# Fritzing sketch Hub (saved by Fritzing 0.9.3b)
circuit board: 6cm x 2.5cm
breadboards: 1

parts:
  J1 = male pin header, 6 pins [form="♂ (male)"]
  S4 = male pin header, 3 pins [form="♂ (male)"]
  S3 = male pin header, 3 pins [form="♂ (male)"]
  S2 = male pin header, 3 pins [form="♂ (male)"]
  S1 = male pin header, 3 pins [form="♂ (male)"]

nets:
  GND: J1.pin1, S4.pin1, S3.pin1, S2.pin1, S1.pin1
  5V: J1.pin2, S4.pin2, S3.pin2, S2.pin2, S1.pin2
  N1: J1.pin3, S1.pin3
  N2: J1.pin4, S2.pin3
  N3: J1.pin5, S3.pin3
  N4: J1.pin6, S4.pin3

notes:
  GND
  VCC
  AIN
  SA1
  SA3
  SA4
  SA2
