# Fritzing sketch Sistema (saved by Fritzing 0.9.3b)
circuit board: 10cm x 6cm
breadboards: 1

parts:
  U1 = atmega328 [package=dip]
  Componente1 = LC Studio SD Card Module
  XTAL1 = Crystal [frequency="16 Mhz" package=THT]
  C2 = Ceramic Capacitor [capacitance=22pF package="100 mil [THT, multilayer]"]
  C3 = Ceramic Capacitor [capacitance=22pF package="100 mil [THT, multilayer]"]
  R1 = Resistor [tolerance=±5% resistance=10k package=THT]
  J3 = male pin header, 2 pins [form="♂ (male)"]
  U2 = Voltage Regulator - 5V [package="TO220 [THT]"]
  Power_plug1 = Power plug
  D1 = Rectifier Diode [part_number=1N4001 package="300 mil [THT]"]
  C5 = Electrolytic Capacitor [capacitance=10µF voltage=20V package="100 mil [THT, electrolytic]"]
  C6 = Electrolytic Capacitor [capacitance=10µF voltage=20V package="100 mil [THT, electrolytic]"]
  Sainda_Bomba = male pin header, 6 pins [form="♂ (male)"]
  J9 = male pin header, 2 pins [form="♂ (male)"]  # not connected
  R2 = Resistor [tolerance=±5% resistance=220 package=THT]
  R3 = Resistor [tolerance=±5% resistance=220 package=THT]
  J7 = male pin header, 6 pins [form="♂ (male)"]
  LED1 = DUO LED RG [package="5 mm [THT]"]
  Reset = Pushbutton [package="[THT]"]
  J2 = male pin header, 5 pins [form="♂ (male)"]
  Tiny_RTC2 = Tiny RTC
  LED2 = LED - 5mm [color="Red (633nm)" package="5 mm [THT]"]
  R4 = Resistor [tolerance=±5% resistance=10k package=THT]

nets (from the schematic view):
  N1: U1.RESET, R1.Pin_0, Reset.Pin_1, Reset.Pin_2
  N2: U1.D0_(RX), J2.pin4
  N3: U1.D1_(TX), J2.pin3
  N4: U1.D4, R3.Pin_1
  5V: U1.VCC, Componente1.5V, R1.Pin_1, U2.output_voltage, C6.+, Sainda_Bomba.pin6, J7.pin6, LED1.common_cathode, J2.pin2, Tiny_RTC2.VCC, R4.Pin_0
  GND: U1.GND, Componente1.GND, C2.1, C3.0, U2.GND, Sainda_Bomba.pin1, J7.pin1, Reset.Pin_3, Reset.Pin_4, J2.pin1, Tiny_RTC2.GND, LED2.cathode
  N5: U1.XLAT1, XTAL1.pin_0, C3.1
  N6: U1.XLAT2, XTAL1.pin_1, C2.0
  N7: U1.D5_(PWM), R2.Pin_0
  N8: U1.D6_(PWM), Sainda_Bomba.pin2
  N9: U1.D7, Sainda_Bomba.pin3
  N10: U1.D8, Sainda_Bomba.pin4
  N11: U1.D9_(PWM), Sainda_Bomba.pin5
  N12: U1.D10_(PWM), Componente1.CS
  N13: U1.D11_(PWM), Componente1.MOSI
  N14: U1.D12, Componente1.MISO
  N15: U1.D13, Componente1.SCK
  N16: U1.A0, J7.pin2
  N17: U1.A1, J7.pin3
  N18: U1.A2, J7.pin4
  N19: U1.A3, J7.pin5
  N20: U1.A4, Tiny_RTC2.SDA
  N21: U1.A5, Tiny_RTC2.SCL#7
  N22: J3.pin1, J2.pin5
  N23: U2.input_voltage, D1.cathode, C5.+
  N24: Power_plug1.GND, C5.-, C6.-
  N25: Power_plug1.VCC, D1.anode
  N26: R2.Pin_1, LED1.red_anode
  N27: R3.Pin_0, LED1.green_anode

custom parts:
  LC Studio SD Card Module: The LC Studio SD card module serves as an interface to an SD card. The module works at 3.3 volts and 5 volts. The SPI (Serial Peripheral Interface) protocol is used for communicating with the module.
  Tiny RTC: Tiny RTC I2C module DS1370Z RTC and AT24C32 EEPROM
